// Logisim project DOT_MATRIX_PRINTER.circ as structural Verilog: 11 circuits, main circuit main
module main (
);

  wire clock_1_out, PAD_ch_pad;
  wire [1:0] _0_out;
  wire [2:0] _1_out, _4_out, _7_out;
  wire [5:0] A_out;
  wire [6:0] PAD_out_6;
  wire [24:0] LOGIC_led_out;

  Clock clock_1 (.out(clock_1_out));
  LOGIC LOGIC (.CHANGE(PAD_ch_pad), .CLK(clock_1_out), .ASCII_In(PAD_out_6), .LED_out(LOGIC_led_out));
  NUM PAD (
    .in_1(_0_out), ._123(_1_out), ._456(_4_out), ._789(_7_out), .L(A_out), .out_6(PAD_out_6),
    .CH_PAD(PAD_ch_pad));
  Button _1 (.out(_1_out[0]));
  Button _4 (.out(_4_out[0]));
  Button _7 (.out(_7_out[0]));
  Button Clr (.out(_0_out[1]));
  Button _2 (.out(_1_out[1]));
  Button _3 (.out(_1_out[2]));
  Button _5 (.out(_4_out[1]));
  Button _6 (.out(_4_out[2]));
  Button _8 (.out(_7_out[1]));
  Button _9 (.out(_7_out[2]));
  Button _0 (.out(_0_out[0]));
  DotMatrix #(.matrixrows(5)) dotmatrix_1 (
    .col0(LOGIC_led_out[24:20]), .col1(LOGIC_led_out[19:15]), .col2(LOGIC_led_out[14:10]),
    .col3(LOGIC_led_out[9:5]), .col4(LOGIC_led_out[4:0]));
  Button A (.out(A_out[0]));
  Button B (.out(A_out[1]));
  Button C (.out(A_out[2]));
  Button D (.out(A_out[3]));
  Button E (.out(A_out[4]));
  Button F (.out(A_out[5]));

  // Notes on the sheet:
  //   INPUTS
  //   OUTPUT(5X5 LED)
endmodule

module SELECT (
  input  [6:0] ASCII_In,
  output NUM_ENABLE,
  output [3:0] NUM_Select,
  output [2:0] LETTER_Select,
  output LETTER_ENABLE
);

  and and_1 (NUM_ENABLE, ~ASCII_In[6], ASCII_In[4]);  // AND_Gate
  nor nor_1 (LETTER_ENABLE, ASCII_In[3], ASCII_In[4]);

  assign LETTER_Select = ASCII_In[2:0];
  assign NUM_Select = ASCII_In[3:0];
endmodule

module Col_1 (
  input  [6:0] Column_1_in,
  output [4:0] Column_1_out
);

  wire decoder_1_out0, decoder_1_out1, decoder_1_out2, decoder_1_out3, decoder_1_out4, decoder_1_out5,
       decoder_1_out6, decoder_1_out7, decoder_1_out8, decoder_1_out9, select_1_letter_enable,
       select_1_num_enable;
  wire [2:0] select_1_letter_select;
  wire [3:0] select_1_num_select;
  wire [5:0] decoder_2_out6;

  SELECT select_1 (
    .ASCII_In(Column_1_in), .NUM_ENABLE(select_1_num_enable), .LETTER_ENABLE(select_1_letter_enable),
    .NUM_Select(select_1_num_select), .LETTER_Select(select_1_letter_select));
  Decoder #(.select(4), .disabled(0)) decoder_1 (
    .out0(decoder_1_out0), .out1(decoder_1_out1), .out2(decoder_1_out2), .out3(decoder_1_out3),
    .out4(decoder_1_out4), .out5(decoder_1_out5), .out6(decoder_1_out6), .out7(decoder_1_out7),
    .out8(decoder_1_out8), .out9(decoder_1_out9), .sel(select_1_num_select), .en(select_1_num_enable));  // open: out10, out11, out12, out13, out14, out15
  Decoder #(.select(3), .disabled(0)) decoder_2 (
    .out1(decoder_2_out6[5]), .out2(decoder_2_out6[4]), .out3(decoder_2_out6[3]), .out4(decoder_2_out6[2]),
    .out5(decoder_2_out6[1]), .out6(decoder_2_out6[0]), .sel(select_1_letter_select),
    .en(select_1_letter_enable));  // open: out0, out7
  or or_1 (Column_1_out[0], decoder_1_out2, decoder_1_out3, decoder_1_out5, decoder_2_out6[5], decoder_2_out6[4], decoder_2_out6[2], decoder_2_out6[1], decoder_2_out6[0]);
  nor nor_1 (Column_1_out[1], decoder_1_out1, decoder_1_out3, decoder_1_out5, decoder_1_out7, decoder_1_out9);
  or or_2 (Column_1_out[2], decoder_1_out0, decoder_1_out5, decoder_1_out6, decoder_2_out6[5], decoder_2_out6[4], decoder_2_out6[3], decoder_2_out6[2], decoder_2_out6[1], decoder_2_out6[0]);
  nor nor_2 (Column_1_out[3], decoder_1_out1, decoder_1_out2, decoder_1_out3, decoder_1_out4, decoder_1_out7, decoder_2_out6[5]);
  or or_3 (Column_1_out[4], decoder_1_out2, decoder_1_out3, decoder_1_out5, decoder_1_out7, decoder_2_out6[4], decoder_2_out6[2], decoder_2_out6[1], decoder_2_out6[0]);

  // Notes on the sheet:
  //   OUTPUT CORRESPONDING 0-9
  //   OUTPUT CORRESPONDING A-F
  //   OUTPUTS FOR ROWS OFCOLUMN 1
endmodule

module Col_2 (
  input  [6:0] Column_2_in,
  output [4:0] COLUMN_2_OUT
);

  wire decoder_1_out0, decoder_1_out1, decoder_1_out2, decoder_1_out3, decoder_1_out4, decoder_1_out5,
       decoder_1_out6, decoder_1_out7, decoder_1_out8, decoder_1_out9, select_1_letter_enable,
       select_1_num_enable;
  wire [2:0] select_1_letter_select;
  wire [3:0] select_1_num_select;
  wire [5:0] decoder_2_out6;

  SELECT select_1 (
    .ASCII_In(Column_2_in), .NUM_ENABLE(select_1_num_enable), .LETTER_ENABLE(select_1_letter_enable),
    .NUM_Select(select_1_num_select), .LETTER_Select(select_1_letter_select));
  Decoder #(.select(4), .disabled(0)) decoder_1 (
    .out0(decoder_1_out0), .out1(decoder_1_out1), .out2(decoder_1_out2), .out3(decoder_1_out3),
    .out4(decoder_1_out4), .out5(decoder_1_out5), .out6(decoder_1_out6), .out7(decoder_1_out7),
    .out8(decoder_1_out8), .out9(decoder_1_out9), .sel(select_1_num_select), .en(select_1_num_enable));  // open: out10, out11, out12, out13, out14, out15
  Decoder #(.select(3), .disabled(0)) decoder_2 (
    .out1(decoder_2_out6[5]), .out2(decoder_2_out6[4]), .out3(decoder_2_out6[3]), .out4(decoder_2_out6[2]),
    .out5(decoder_2_out6[1]), .out6(decoder_2_out6[0]), .sel(select_1_letter_select),
    .en(select_1_letter_enable));  // open: out0, out7
  nor nor_1 (COLUMN_2_OUT[0], decoder_1_out4, decoder_2_out6[0], decoder_2_out6[5]);
  or or_1 (COLUMN_2_OUT[1], decoder_1_out4, decoder_2_out6[5]);
  or or_2 (COLUMN_2_OUT[3], decoder_1_out1, decoder_2_out6[5]);
  nor nor_2 (COLUMN_2_OUT[2], decoder_1_out0, decoder_1_out1, decoder_1_out7, decoder_2_out6[5], decoder_2_out6[3], decoder_2_out6[2]);
  nor nor_3 (COLUMN_2_OUT[4], decoder_1_out1, decoder_1_out4, decoder_2_out6[5]);

  // Notes on the sheet:
  //   LOGIC
  //   OUTPUT CORRESPONDING 0-9
  //   OUTPUT CORRESPONDING A-F
  //   OUTPUT FOR ROWS OF 2ND COLUMN
endmodule

module Col_3 (
  input  [6:0] Column_3_in,
  output [4:0] Column_3_out,
  output VALID_LOW
);

  wire decoder_1_out0, decoder_1_out1, decoder_1_out2, decoder_1_out3, decoder_1_out4, decoder_1_out5,
       decoder_1_out6, decoder_1_out7, decoder_1_out8, decoder_1_out9, or_4_out, select_1_letter_enable,
       select_1_num_enable;
  wire [2:0] select_1_letter_select;
  wire [3:0] select_1_num_select;
  wire [5:0] decoder_2_out6;

  SELECT select_1 (
    .ASCII_In(Column_3_in), .NUM_ENABLE(select_1_num_enable), .LETTER_ENABLE(select_1_letter_enable),
    .NUM_Select(select_1_num_select), .LETTER_Select(select_1_letter_select));
  Decoder #(.select(4), .disabled(0)) decoder_1 (
    .out0(decoder_1_out0), .out1(decoder_1_out1), .out2(decoder_1_out2), .out3(decoder_1_out3),
    .out4(decoder_1_out4), .out5(decoder_1_out5), .out6(decoder_1_out6), .out7(decoder_1_out7),
    .out8(decoder_1_out8), .out9(decoder_1_out9), .sel(select_1_num_select), .en(select_1_num_enable));  // open: out10, out11, out12, out13, out14, out15
  Decoder #(.select(3), .disabled(0)) decoder_2 (
    .out1(decoder_2_out6[5]), .out2(decoder_2_out6[4]), .out3(decoder_2_out6[3]), .out4(decoder_2_out6[2]),
    .out5(decoder_2_out6[1]), .out6(decoder_2_out6[0]), .sel(select_1_letter_select),
    .en(select_1_letter_enable));  // open: out0, out7
  or or_1 (Column_3_out[1], decoder_1_out1, decoder_1_out4, decoder_2_out6[5], decoder_1_out7);
  or or_2 (Column_3_out[3], decoder_1_out1, decoder_1_out4);
  or or_3 (Column_3_out[4], decoder_2_out6[2], decoder_1_out0, decoder_1_out1, decoder_1_out2, decoder_1_out3, decoder_1_out5, decoder_1_out6, decoder_2_out6[1], decoder_1_out7, decoder_1_out8, decoder_1_out9, decoder_2_out6[5], decoder_2_out6[4], decoder_2_out6[3], decoder_2_out6[0]);
  nor nor_1 (Column_3_out[0], decoder_1_out7, decoder_2_out6[5], decoder_2_out6[0], decoder_1_out4);
  nor nor_2 (Column_3_out[2], decoder_1_out4, decoder_1_out7, decoder_2_out6[5], decoder_2_out6[3], decoder_2_out6[2], decoder_1_out0);
  or or_4 (or_4_out, Column_3_out[3], Column_3_out[4]);
  not not_1 (VALID_LOW, or_4_out);

  // Notes on the sheet:
  //   LOGIC
  //   OUTPUT CORRESPONDING 0-9
  //   OUTPUT CORRESPONDING A-F
  //   OUTPUT FOR ROWS OF COLUMN 3
endmodule

module Col_4 (
  input  [6:0] Column_4_in,
  output [4:0] Column_4_out
);

  wire decoder_1_out0, decoder_1_out1, decoder_1_out2, decoder_1_out3, decoder_1_out4, decoder_1_out5,
       decoder_1_out6, decoder_1_out7, decoder_1_out8, decoder_1_out9, select_1_letter_enable,
       select_1_num_enable;
  wire [2:0] select_1_letter_select;
  wire [3:0] select_1_num_select;
  wire [5:0] decoder_2_out6;

  SELECT select_1 (
    .ASCII_In(Column_4_in), .NUM_ENABLE(select_1_num_enable), .LETTER_ENABLE(select_1_letter_enable),
    .NUM_Select(select_1_num_select), .LETTER_Select(select_1_letter_select));
  Decoder #(.select(4), .disabled(0)) decoder_1 (
    .out0(decoder_1_out0), .out1(decoder_1_out1), .out2(decoder_1_out2), .out3(decoder_1_out3),
    .out4(decoder_1_out4), .out5(decoder_1_out5), .out6(decoder_1_out6), .out7(decoder_1_out7),
    .out8(decoder_1_out8), .out9(decoder_1_out9), .sel(select_1_num_select), .en(select_1_num_enable));  // open: out10, out11, out12, out13, out14, out15
  Decoder #(.select(3), .disabled(0)) decoder_2 (
    .out1(decoder_2_out6[5]), .out2(decoder_2_out6[4]), .out3(decoder_2_out6[3]), .out4(decoder_2_out6[2]),
    .out5(decoder_2_out6[1]), .out6(decoder_2_out6[0]), .sel(select_1_letter_select),
    .en(select_1_letter_enable));  // open: out0, out7
  or or_1 (Column_4_out[1], decoder_1_out4, decoder_2_out6[5]);
  or or_2 (Column_4_out[3], decoder_1_out4, decoder_2_out6[5]);
  nor nor_1 (Column_4_out[0], decoder_1_out7, decoder_2_out6[5], decoder_2_out6[0]);
  nor nor_2 (Column_4_out[2], decoder_1_out0, decoder_1_out1, decoder_2_out6[5], decoder_2_out6[3], decoder_2_out6[2]);
  nor nor_3 (Column_4_out[4], decoder_1_out1, decoder_2_out6[5]);

  // Notes on the sheet:
  //   LOGIC
  //   OUTPUTS CORRESPONDING 0-9
  //   OUTPUTS CORRESPONDING A-F
  //   OUTPUTS FOR ROWS OF COLUMN 4
endmodule

module Col_5 (
  input  [6:0] Column_1_in,
  output [4:0] Column_1_out
);

  wire decoder_1_out0, decoder_1_out1, decoder_1_out2, decoder_1_out3, decoder_1_out4, decoder_1_out5,
       decoder_1_out6, decoder_1_out7, decoder_1_out8, decoder_1_out9, select_1_letter_enable,
       select_1_num_enable;
  wire [2:0] select_1_letter_select;
  wire [3:0] select_1_num_select;
  wire [5:0] decoder_2_out6;

  SELECT select_1 (
    .ASCII_In(Column_1_in), .NUM_ENABLE(select_1_num_enable), .LETTER_ENABLE(select_1_letter_enable),
    .NUM_Select(select_1_num_select), .LETTER_Select(select_1_letter_select));
  Decoder #(.select(4), .disabled(0)) decoder_1 (
    .out0(decoder_1_out0), .out1(decoder_1_out1), .out2(decoder_1_out2), .out3(decoder_1_out3),
    .out4(decoder_1_out4), .out5(decoder_1_out5), .out6(decoder_1_out6), .out7(decoder_1_out7),
    .out8(decoder_1_out8), .out9(decoder_1_out9), .sel(select_1_num_select), .en(select_1_num_enable));  // open: out10, out11, out12, out13, out14, out15
  Decoder #(.select(3), .disabled(0)) decoder_2 (
    .out1(decoder_2_out6[5]), .out2(decoder_2_out6[4]), .out3(decoder_2_out6[3]), .out4(decoder_2_out6[2]),
    .out5(decoder_2_out6[1]), .out6(decoder_2_out6[0]), .sel(select_1_letter_select),
    .en(select_1_letter_enable));  // open: out0, out7
  or or_1 (Column_1_out[0], decoder_1_out2, decoder_2_out6[5], decoder_1_out5);
  nor nor_1 (Column_1_out[1], decoder_1_out1, decoder_1_out2, decoder_1_out7, decoder_2_out6[3], decoder_2_out6[1], decoder_2_out6[0]);
  or or_2 (Column_1_out[2], decoder_1_out0, decoder_1_out5, decoder_1_out9, decoder_2_out6[5], decoder_2_out6[2]);
  or or_3 (Column_1_out[3], decoder_1_out2, decoder_1_out3, decoder_1_out7, decoder_1_out8, decoder_1_out9, decoder_2_out6[4], decoder_2_out6[2], decoder_1_out0);
  or or_4 (Column_1_out[4], decoder_1_out5, decoder_1_out7);

  // Notes on the sheet:
  //   LOGIC
  //   OUTPUTS CORRESPONDING 0-9
  //   OUTPUT CORRESPONDING A-F
  //   OUTPUTS FOR ROWS OF COLUMN 5
endmodule

module NUM (
  input  [1:0] in_1,
  input  [2:0] _123,
  input  [2:0] _456,
  input  [2:0] _789,
  input  [5:0] L,
  output [6:0] out_6,
  output CH_PAD
);

  wire priority_encoder_1_en_out, priority_encoder_1_gs, priority_encoder_2_en_out, priority_encoder_2_gs;
  wire [3:0] multiplexer_1_out, priority_encoder_1_out, priority_encoder_2_out;

  Priority_Encoder #(.select(4)) priority_encoder_1 (
    .in0(in_1[0]), .in1(_123[0]), .in2(_123[1]), .in3(_123[2]), .in4(_456[0]), .in5(_456[1]), .in6(_456[2]),
    .in7(_789[0]), .in8(_789[1]), .in9(_789[2]), .in10(in_1[1]), .out(priority_encoder_1_out),
    .gs(priority_encoder_1_gs), .en_out(priority_encoder_1_en_out));  // open: in11, in12, in13, in14, in15, en_in
  Priority_Encoder #(.select(4)) priority_encoder_2 (
    .in1(L[0]), .in2(L[1]), .in3(L[2]), .in4(L[3]), .in5(L[4]), .in6(L[5]), .out(priority_encoder_2_out),
    .gs(priority_encoder_2_gs), .en_out(priority_encoder_2_en_out));  // open: in0, in7, in8, in9, in10, in11, in12, in13, in14, in15, en_in
  Multiplexer #(.width(4), .enable("false")) multiplexer_1 (
    .in0(priority_encoder_1_out), .in1(priority_encoder_2_out), .out(multiplexer_1_out),
    .sel(priority_encoder_1_en_out));
  or or_1 (CH_PAD, priority_encoder_1_gs, priority_encoder_2_gs);
  Register #(.width(4), .trigger("falling")) register_1 (
    .D(multiplexer_1_out), .Q(out_6[3:0]), .clk(CH_PAD));  // open: en, clr
  D_Flip_Flop d_ff_1 (.clk(CH_PAD), .D(priority_encoder_2_en_out), .Q(out_6[4]));  // open: Qn, preset, en, reset

  assign out_6[6:5] = 2'b00;
endmodule

module KEYBORD (
  input  [6:0] ASCII_In,
  input  CLOCK,
  input  Buffer,
  input  ENTER,
  output B_ESC,
  output [6:0] out_6,
  output CH__KEY
);

  wire and_1_out, and_2_out, not_1_out, t_ff_1_q;
  wire [2:0] counter_1_q;

  Counter #(.width(3), .max('h7)) counter_1 (.Q(counter_1_q), .clk(CLOCK), .clr(ENTER));  // open: load, D, count, carry
  and and_1 (and_1_out, counter_1_q[0], ~counter_1_q[1], ~counter_1_q[2]);  // AND_Gate
  and and_2 (and_2_out, and_1_out, t_ff_1_q);
  T_Flip_Flop t_ff_1 (.clk(ENTER), .T(ENTER), .Q(t_ff_1_q), .reset(not_1_out));  // open: Qn, preset, en
  assign B_ESC = Buffer ? and_2_out : 1'bz;  // Controlled_Buffer controlled_buffer_1
  not not_1 (not_1_out, Buffer);
  Register #(.width(7)) register_1 (.D(ASCII_In), .Q(out_6), .clk(CH__KEY));  // open: en, clr
  and and_3 (CH__KEY, Buffer, and_2_out);
endmodule

module LOGIC (
  input  CLK,
  input  CHANGE,
  input  [6:0] ASCII_In,
  output [24:0] LED_out
);

  wire COL_3_valid_low, RING_CTR__0, RING_CTR__5, RING_CTR_out_4, RING_CTR_out_5, RING_CTR_out_6;
  wire [4:0] COL_1_column_1_out, COL_2_column_2_out, COL_3_column_3_out, COL_4_column_4_out,
       COL_5_column_1_out, multiplexer_1_out, multiplexer_2_out, multiplexer_3_out, multiplexer_4_out,
       multiplexer_5_out;

  Col_1 COL_1 (.Column_1_in(ASCII_In), .Column_1_out(COL_1_column_1_out));
  Col_2 COL_2 (.Column_2_in(ASCII_In), .COLUMN_2_OUT(COL_2_column_2_out));
  Col_3 COL_3 (.Column_3_in(ASCII_In), .Column_3_out(COL_3_column_3_out), .VALID_LOW(COL_3_valid_low));
  Col_4 COL_4 (.Column_4_in(ASCII_In), .Column_4_out(COL_4_column_4_out));
  Col_5 COL_5 (.Column_1_in(ASCII_In), .Column_1_out(COL_5_column_1_out));
  Multiplexer #(.width(5), .enable("false")) multiplexer_1 (
    .in0(COL_1_column_1_out), .in1({5{1'b0}}), .out(multiplexer_1_out), .sel(COL_3_valid_low));
  Multiplexer #(.width(5), .enable("false")) multiplexer_2 (
    .in0(COL_2_column_2_out), .in1(5'b00100), .out(multiplexer_2_out), .sel(COL_3_valid_low));
  Multiplexer #(.width(5), .enable("false")) multiplexer_3 (
    .in0(COL_3_column_3_out), .in1(5'b00100), .out(multiplexer_3_out), .sel(COL_3_valid_low));
  Multiplexer #(.width(5), .enable("false")) multiplexer_4 (
    .in0(COL_4_column_4_out), .in1(5'b00100), .out(multiplexer_4_out), .sel(COL_3_valid_low));
  Multiplexer #(.width(5), .enable("false")) multiplexer_5 (
    .in0(COL_5_column_1_out), .in1({5{1'b0}}), .out(multiplexer_5_out), .sel(COL_3_valid_low));
  RING_CTR RING_CTR (
    .CLK(CLK), .RESET(CHANGE), ._0(RING_CTR__0), .out_4(RING_CTR_out_4), .out_5(RING_CTR_out_5),
    .out_6(RING_CTR_out_6), ._5(RING_CTR__5));
  Register #(.width(5), .trigger("falling")) register_1 (
    .D(multiplexer_1_out), .Q(LED_out[24:20]), .clk(RING_CTR__0), .clr(CHANGE));  // open: en
  Register #(.width(5), .trigger("falling")) register_2 (
    .D(multiplexer_2_out), .Q(LED_out[19:15]), .clk(RING_CTR_out_4), .clr(CHANGE));  // open: en
  Register #(.width(5), .trigger("falling")) register_3 (
    .D(multiplexer_3_out), .Q(LED_out[14:10]), .clk(RING_CTR_out_5), .clr(CHANGE));  // open: en
  Register #(.width(5), .trigger("falling")) register_4 (
    .D(multiplexer_4_out), .Q(LED_out[9:5]), .clk(RING_CTR_out_6), .clr(CHANGE));  // open: en
  Register #(.width(5), .trigger("falling")) register_5 (
    .D(multiplexer_5_out), .Q(LED_out[4:0]), .clk(RING_CTR__5), .clr(CHANGE));  // open: en
endmodule

module RING_CTR (
  input  CLK,
  input  RESET,
  output _0,
  output out_4,
  output out_5,
  output out_6,
  output _5
);

  wire and_1_out, d_ff_6_q;

  and and_1 (and_1_out, CLK, ~d_ff_6_q);  // AND_Gate
  D_Flip_Flop d_ff_1 (.clk(and_1_out), .D(d_ff_6_q), .Q(_0), .preset(RESET));  // open: Qn, en, reset
  D_Flip_Flop d_ff_2 (.clk(and_1_out), .D(_0), .Q(out_4), .reset(RESET));  // open: Qn, preset, en
  D_Flip_Flop d_ff_3 (.clk(and_1_out), .D(out_5), .Q(out_6), .reset(RESET));  // open: Qn, preset, en
  D_Flip_Flop d_ff_4 (.clk(and_1_out), .D(out_4), .Q(out_5), .reset(RESET));  // open: Qn, preset, en
  D_Flip_Flop d_ff_5 (.clk(and_1_out), .D(out_6), .Q(_5), .reset(RESET));  // open: Qn, preset, en
  D_Flip_Flop d_ff_6 (.clk(and_1_out), .D(_5), .Q(d_ff_6_q), .reset(RESET));  // open: Qn, preset, en
endmodule
